# Fritzing sketch Sketch (saved by Fritzing 0.9.5d)
breadboards: 1

parts:
  ZS-042_RTC1 = ZS-042 RTC Module
  S1 = Pushbutton [package="[SMD]"]
  S2 = Pushbutton [package="[SMD]"]
  S3 = Pushbutton [package="[SMD]"]
  S4 = Pushbutton [package="[SMD]"]
  RHT1 = Humidity and Temperature Sensor RHT03
  Дисплей = Adafruit 1.44 inch TFT Breakout [part_number="Adafruit #2088"]
  Buzzer1 = Buzzer
  Arduino_UNO = Arduino Uno (Rev3)

nets:
  GND: ZS-042_RTC1.GND, S1.Pin_3, S1.Pin_4, S2.Pin_3, S2.Pin_4, S3.Pin_3, S3.Pin_4, S4.Pin_3, S4.Pin_4, RHT1.GND_2, Дисплей.GND, Buzzer1.pin2, Arduino_UNO.GND
  VCC: ZS-042_RTC1.VCC, RHT1.Vcc, Дисплей.VIN, Arduino_UNO.5V
  N1: ZS-042_RTC1.SDA, Arduino_UNO.A4/SDA
  N2: ZS-042_RTC1.SCL, Arduino_UNO.A5/SCL
  N3: ZS-042_RTC1.SQW, Arduino_UNO.D2
  N4: S1.Pin_1, S1.Pin_2, Arduino_UNO.A0
  N5: S2.Pin_1, S2.Pin_2, Arduino_UNO.A1
  N6: S3.Pin_1, S3.Pin_2, Arduino_UNO.A2
  N7: S4.Pin_1, S4.Pin_2, Arduino_UNO.A3
  N8: RHT1.Data-signal, Arduino_UNO.D6_PWM
  N9: Дисплей.SCK, Arduino_UNO.D13/SCK
  N10: Дисплей.TFTCS, Arduino_UNO.D11_PWM/MOSI
  N11: Дисплей.RESET, Arduino_UNO.D9_PWM
  N12: Дисплей.TFTDC, Arduino_UNO.D8
  N13: Дисплей.CARDCS, Arduino_UNO.D10_PWM/SS
  N14: Buzzer1.pin1, Arduino_UNO.D4

custom parts:
  Adafruit 1.44 inch TFT Breakout: This lovely little display breakout is the best way to add a small, colorful and bright display to any project. Since the display uses 4-wire SPI to communicate and has its own pixel-addressable frame buffer, it can be used with every kind of microcontroller. Even a very small one with low memory and few pins available! The 1.44" display has 128x128 color pixels. Unlike the low cost "Nokia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
